# Fritzing sketch UGV_Indoor_PCB (saved by Fritzing 0.9.6b)
breadboards: 1

parts:
  U1 = NodeMCU V1.0
  U2 = LM2596 step down module
  IC1 = L293D [package=THT]
  M1 = gear-motor
  M2 = gear-motor
  U3 = LIPO-2000mAh [package=lipo-2000]
  U4 = SWITCH-SPST-2 [package=switch-spst-vertical]

nets:
  N1: U1.D1, IC1.Enable_1
  N2: U1.D2, IC1.In_1
  N3: U1.D3, IC1.In_2
  N4: U1.GND, U2.IN-, U2.OUT-, U3.-
  N5: U1.D5, IC1.Enable_2
  N6: U1.D6, IC1.In_4
  N7: U1.D7, IC1.In_3
  N8: U1.Vin, U2.OUT+, IC1.+V
  N9: U2.IN+, IC1.+Vmotor, U4.O
  N10: IC1.Out_1_(_Controlled_by_Enable_1_), M1.pin_1
  N11: IC1.Out_2_(_Controlled_by_Enable_1_), M1.pin_2
  N12: IC1.Out_3_(_Controlled_by_Enable_2_), M2.pin_2
  N13: IC1.Out_4_(_Controlled_by_Enable_2_), M2.pin_1
  N14: U3.+, U4.P

custom parts:
  NodeMCU V1.0: ESP8266 based NodeMCU
  LM2596 step down module: LM2596 DC-DC step down power supply module 3 A.
